# Fritzing sketch analogSensorThresh2xLED (saved by Fritzing 0.9.10b)
breadboards: 1

parts:
  A1 = Arduino UNO R4 WiFi
  R1 = Rotary Potentiometer (Small) [maximum_resistance=100kΩ knob_status=50% power=0.5W package=THT]
  LED1 = LED - 5mm [color="Red (633nm)" current=0.030 package="5 mm [THT]"]  # not connected
  R2 = Resistor [tolerance=±5% power=0.25 resistance=220 package=THT]
  R3 = Resistor [tolerance=±5% power=0.25 resistance=220 package=THT]
  LED2 = LED - 5mm [color="Red (633nm)" current=0.030 package="5 mm [THT]"]

nets:
  N1: A1.Pin_7, A1.Pin_19, R1.leg2
  N2: A1.Pin_9, A1.Pin_30, R1.leg1, R2.Pin_1, R3.Pin_1
  N3: A1.Pin_12, R1.wiper
  N4: A1.Pin_46, LED2.anode
  N5: R3.Pin_0, LED2.cathode

custom parts:
  Arduino UNO R4 WiFi: The Arduino UNO R4 WiFi merges the RA4M1 microprocessor from Renesas with the ESP32-S3 from Espressif, creating an all-in-one tool for makers with enhanced processing power and a diverse array of new peripherals.
