# Fritzing sketch blinkExternalLED2 (saved by Fritzing 0.9.10b)
breadboards: 1

parts:
  A1 = Arduino UNO R4 WiFi
  LED1 = smd LED [color="Red (633nm)" package="1206 [SMD]"]
  R1 = Resistor [tolerance=±5% resistance=220 package="2010 [SMD]"]

nets:
  N1: A1.Pin_9, A1.Pin_30, LED1.cathode
  N2: A1.Pin_47, R1.Pin_0
  N3: LED1.anode, R1.Pin_1

custom parts:
  Arduino UNO R4 WiFi: The Arduino UNO R4 WiFi merges the RA4M1 microprocessor from Renesas with the ESP32-S3 from Espressif, creating an all-in-one tool for makers with enhanced processing power and a diverse array of new peripherals.
