# Fritzing sketch ldrSensor (saved by Fritzing 0.9.10b)
breadboards: 1

parts:
  A1 = Arduino UNO R4 WiFi
  R1 = Resistor [tolerance=±5% resistance=10k package="1206 [SMD]"]
  R2 = Photocell (LDR) [package=THT]

nets:
  N1: A1.Pin_7, A1.Pin_19, R2.pin_1
  N2: A1.Pin_9, A1.Pin_30, R1.Pin_0
  N3: A1.Pin_12, R1.Pin_1, R2.pin_0

custom parts:
  Arduino UNO R4 WiFi: The Arduino UNO R4 WiFi merges the RA4M1 microprocessor from Renesas with the ESP32-S3 from Espressif, creating an all-in-one tool for makers with enhanced processing power and a diverse array of new peripherals.
